# Fritzing sketch RFID - LED (saved by Fritzing 0.9.3b)
breadboards: 1

parts:
  Part1 = Arduino Uno (Rev3)
  Part2 = RFID-RC522-v2
  R1 = Resistor [tolerance=±5% resistance=220 package=THT]
  R2 = Resistor [tolerance=±5% resistance=220 package=THT]
  R3 = Resistor [tolerance=±5% resistance=220 package=THT]
  R4 = Resistor [tolerance=±5% resistance=220 package=THT]
  R5 = Resistor [tolerance=±5% resistance=220 package=THT]
  R6 = Resistor [tolerance=±5% resistance=220 package=THT]
  LED4 = LED - 5mm [color="Red (633nm)" package="5 mm [THT]"]
  LED1 = LED - 5mm [color="Red (633nm)" package="5 mm [THT]"]
  LED5 = LED - 5mm [color="Red (633nm)" package="5 mm [THT]"]
  LED6 = LED - 5mm [color="Red (633nm)" package="5 mm [THT]"]
  LED2 = LED - 5mm [color="Red (633nm)" package="5 mm [THT]"]
  LED3 = LED - 5mm [color="Red (633nm)" package="5 mm [THT]"]
  Part3 = Arduino Uno (Rev3)
  VCC2 = Battery
  U2 = RELAY [package=relay-jzc]
  L1 = Solenoid

nets:
  N1: Part1.D9_PWM, Part2.RST
  N2: Part1.D10_PWM/SS, Part2.SDA
  N3: Part1.D11_PWM/MOSI, Part2.MOSI
  N4: Part1.D12/MISO, Part2.MISO
  N5: Part1.D13/SCK, Part2.SCK
  3V3: Part1.3V3, Part2.3.3V
  GND: Part1.GND, Part2.GND
  N6: R1.Pin_0, LED1.anode
  N7: R1.Pin_1, Part3.D4
  N8: R2.Pin_0, LED2.anode
  N9: R2.Pin_1, Part3.D3_PWM
  N10: R3.Pin_0, LED3.anode
  N11: R3.Pin_1, Part3.D2
  N12: R4.Pin_0, LED4.anode
  N13: R4.Pin_1, Part3.D7
  N14: R5.Pin_0, LED5.anode
  N15: R5.Pin_1, Part3.D6_PWM
  N16: R6.Pin_0, LED6.anode
  N17: R6.Pin_1, Part3.D5_PWM
  N18: LED4.cathode, LED1.cathode, LED5.cathode, LED6.cathode, LED2.cathode, LED3.cathode, Part3.GND
  N19: VCC2.-, U2.GND, L1.pin1
  N20: VCC2.+, U2.COM, U2.VCC
  N21: U2.NO, L1.pin2

notes:
  Flash it with arduino code in arduino folder
  Flash it with firrmata
  12V Power Source
  Solenoid Lock Door
  Relay
  RFID Reader

custom parts:
  RFID-RC522-v2: A simple China made RFID-RC522 Reader; do check the pin labels, as this is a MFRC522 based clone.
  RELAY: SPDT relay (COM-00101)
